// Logisim project HSGPRO400.circ as structural Verilog: 18 circuits, main circuit Datapath
module Datapath (
  input  Reset,
  output Overflow
);

  wire Branch, Clock, F7, Imm_Enable, Load, Reg_Disable, Store;
  wire [2:0] Func3;
  wire [4:0] RD, RS1, RS2;
  wire [6:0] Func7, Opcode;
  wire [11:0] Immediate;
  wire [19:0] U_Immediate;
  wire [23:0] extender_1_out;
  wire [31:0] adder_1_out_3, alu_1_out, imm_generator_1_immout, multiplexer_1_out, multiplexer_2_out, PC,
       pc_1_out, ram_1_data, register_file_1_rs1, rom_1_data, StoreD;

  Register #(.width(32)) register_1 (.D(adder_1_out_3), .Q(PC), .clk(Clock), .clr(Reset));  // open: en
  Extender extender_1 (.in(PC), .out(extender_1_out));
  PC pc_1 (.Imm(Immediate), .U_Imm(U_Immediate), .out(pc_1_out), .Opcode(Opcode));
  Clock u_Clock (.out(Clock));
  Adder adder_1 (.in_1(pc_1_out), .in_2(PC), .out_3(adder_1_out_3));
  ROM #(.addrWidth(24), .dataWidth(32)) rom_1 (.addr(extender_1_out), .data(rom_1_data));  // open: sel
  Instruction_decoder instruction_decoder_1 (
    .OPcode(Opcode), .RD(RD), .Func3(Func3), .Rs1(RS1), .Rs2(RS2), .Func7(Func7), .Instruction(rom_1_data),
    .Imm(Immediate), .U_Imm(U_Immediate), .PC(PC));
  // Probe on RD
  // Probe on RS1
  // Probe on RS2
  Control_Unit control_unit_1 (
    .Opcode(Opcode), .Reg_Disable(Reg_Disable), .Imm_Enable(Imm_Enable), .Branch(Branch), .Func7(Func7),
    .out(F7), .Load(Load), .Store(Store));
  Register_File register_file_1 (
    .Clock(Clock), .Clear(Reset), .Rs1(register_file_1_rs1), .Rs2(StoreD), .RW(multiplexer_2_out), .Rd(RD),
    .rs1_Select(RS1), .rs2_Select(RS2), .Enable(Reg_Disable));
  IMM_Generator imm_generator_1 (
    .imm(Immediate), .U_imm(U_Immediate), .PC(PC), .Opcode(Opcode), .ImmOut(imm_generator_1_immout));
  ALU alu_1 (
    .Func7(F7), .Rs1(register_file_1_rs1), .Rs2(multiplexer_1_out), .Out(alu_1_out), .Opcode(Opcode),
    .overflow(Overflow), .Func3(Func3), .Does_B(Branch));
  Multiplexer #(.width(32), .enable("false")) multiplexer_1 (
    .in0(StoreD), .in1(imm_generator_1_immout), .out(multiplexer_1_out), .sel(Imm_Enable));
  RAM #(.addrWidth(24), .dataWidth(32), .bus("separate")) ram_1 (
    .addr(alu_1_out[23:0]), .din(StoreD), .data(ram_1_data), .str(Store), .clk(Clock), .ld(Load));  // open: sel, clr
  Multiplexer #(.width(32), .enable("false")) multiplexer_2 (
    .in0(alu_1_out), .in1(ram_1_data), .out(multiplexer_2_out), .sel(Load));

  // Notes on the sheet:
  //   contents of rom_1 (hex, n*v repeats v):
  //   500093 500113 208463 500193 500213 12b7 102023 2303
endmodule

module Register_File (
  input  [31:0] RW,
  input  Enable,
  input  [4:0] rs1_Select,
  input  [4:0] Rd,
  input  Clock,
  input  Clear,
  input  [4:0] rs2_Select,
  output [31:0] Rs1,
  output [31:0] Rs2
);

  wire demultiplexer_1_out0, demultiplexer_1_out1, demultiplexer_1_out2, demultiplexer_1_out3,
       demultiplexer_1_out4, demultiplexer_1_out5, demultiplexer_1_out6, demultiplexer_1_out7,
       demultiplexer_1_out8, demultiplexer_1_out9, demultiplexer_1_out10, demultiplexer_1_out11,
       demultiplexer_1_out12, demultiplexer_1_out13, demultiplexer_1_out14, demultiplexer_1_out15,
       demultiplexer_1_out16, demultiplexer_1_out17, demultiplexer_1_out18, demultiplexer_1_out19,
       demultiplexer_1_out20, demultiplexer_1_out21, demultiplexer_1_out22, demultiplexer_1_out23,
       demultiplexer_1_out24, demultiplexer_1_out25, demultiplexer_1_out26, demultiplexer_1_out27,
       demultiplexer_1_out28, demultiplexer_1_out29, demultiplexer_1_out30, demultiplexer_1_out31,
       multiplexer_1_out;
  wire [31:0] register_1_q, register_2_q, register_3_q, register_4_q, register_5_q, register_6_q,
       register_7_q, register_8_q, register_9_q, register_10_q, register_11_q, register_12_q, register_13_q,
       register_14_q, register_15_q, register_16_q, register_17_q, register_18_q, register_19_q,
       register_20_q, register_21_q, register_22_q, register_23_q, register_24_q, register_25_q,
       register_26_q, register_27_q, register_28_q, register_29_q, register_30_q, register_31_q,
       register_32_q;

  Multiplexer #(.enable("false")) multiplexer_1 (.in0(1'b1), .in1(1'b0), .out(multiplexer_1_out), .sel(Enable));
  Demultiplexer #(.select(5), .enable("false")) demultiplexer_1 (
    .out0(demultiplexer_1_out0), .out1(demultiplexer_1_out1), .out2(demultiplexer_1_out2),
    .out3(demultiplexer_1_out3), .out4(demultiplexer_1_out4), .out5(demultiplexer_1_out5),
    .out6(demultiplexer_1_out6), .out7(demultiplexer_1_out7), .out8(demultiplexer_1_out8),
    .out9(demultiplexer_1_out9), .out10(demultiplexer_1_out10), .out11(demultiplexer_1_out11),
    .out12(demultiplexer_1_out12), .out13(demultiplexer_1_out13), .out14(demultiplexer_1_out14),
    .out15(demultiplexer_1_out15), .out16(demultiplexer_1_out16), .out17(demultiplexer_1_out17),
    .out18(demultiplexer_1_out18), .out19(demultiplexer_1_out19), .out20(demultiplexer_1_out20),
    .out21(demultiplexer_1_out21), .out22(demultiplexer_1_out22), .out23(demultiplexer_1_out23),
    .out24(demultiplexer_1_out24), .out25(demultiplexer_1_out25), .out26(demultiplexer_1_out26),
    .out27(demultiplexer_1_out27), .out28(demultiplexer_1_out28), .out29(demultiplexer_1_out29),
    .out30(demultiplexer_1_out30), .out31(demultiplexer_1_out31), .in(multiplexer_1_out), .sel(Rd));
  Register #(.width(32)) register_1 (
    .D({32{1'b0}}), .en(demultiplexer_1_out0), .Q(register_1_q), .clk(Clock), .clr(Clear));
  Register #(.width(32)) register_2 (.D(RW), .en(demultiplexer_1_out1), .Q(register_2_q), .clk(Clock), .clr(Clear));
  Register #(.width(32)) register_3 (.D(RW), .en(demultiplexer_1_out2), .Q(register_3_q), .clk(Clock), .clr(Clear));
  Register #(.width(32)) register_4 (.D(RW), .en(demultiplexer_1_out3), .Q(register_4_q), .clk(Clock), .clr(Clear));
  Register #(.width(32)) register_5 (.D(RW), .en(demultiplexer_1_out4), .Q(register_5_q), .clk(Clock), .clr(Clear));
  Register #(.width(32)) register_6 (.D(RW), .en(demultiplexer_1_out5), .Q(register_6_q), .clk(Clock), .clr(Clear));
  Register #(.width(32)) register_7 (.D(RW), .en(demultiplexer_1_out6), .Q(register_7_q), .clk(Clock), .clr(Clear));
  Register #(.width(32)) register_8 (.D(RW), .en(demultiplexer_1_out7), .Q(register_8_q), .clk(Clock), .clr(Clear));
  Register #(.width(32)) register_9 (.D(RW), .en(demultiplexer_1_out8), .Q(register_9_q), .clk(Clock), .clr(Clear));
  Register #(.width(32)) register_10 (.D(RW), .en(demultiplexer_1_out9), .Q(register_10_q), .clk(Clock), .clr(Clear));
  Register #(.width(32)) register_11 (.D(RW), .en(demultiplexer_1_out10), .Q(register_11_q), .clk(Clock), .clr(Clear));
  Register #(.width(32)) register_12 (.D(RW), .en(demultiplexer_1_out11), .Q(register_12_q), .clk(Clock), .clr(Clear));
  Register #(.width(32)) register_13 (.D(RW), .en(demultiplexer_1_out12), .Q(register_13_q), .clk(Clock), .clr(Clear));
  Register #(.width(32)) register_14 (.D(RW), .en(demultiplexer_1_out13), .Q(register_14_q), .clk(Clock), .clr(Clear));
  Register #(.width(32)) register_15 (.D(RW), .en(demultiplexer_1_out14), .Q(register_15_q), .clk(Clock), .clr(Clear));
  Register #(.width(32)) register_16 (.D(RW), .en(demultiplexer_1_out15), .Q(register_16_q), .clk(Clock), .clr(Clear));
  Register #(.width(32)) register_17 (.D(RW), .en(demultiplexer_1_out16), .Q(register_17_q), .clk(Clock), .clr(Clear));
  Register #(.width(32)) register_18 (.D(RW), .en(demultiplexer_1_out17), .Q(register_18_q), .clk(Clock), .clr(Clear));
  Register #(.width(32)) register_19 (.D(RW), .en(demultiplexer_1_out18), .Q(register_19_q), .clk(Clock), .clr(Clear));
  Register #(.width(32)) register_20 (.D(RW), .en(demultiplexer_1_out19), .Q(register_20_q), .clk(Clock), .clr(Clear));
  Register #(.width(32)) register_21 (.D(RW), .en(demultiplexer_1_out20), .Q(register_21_q), .clk(Clock), .clr(Clear));
  Register #(.width(32)) register_22 (.D(RW), .en(demultiplexer_1_out21), .Q(register_22_q), .clk(Clock), .clr(Clear));
  Register #(.width(32)) register_23 (.D(RW), .en(demultiplexer_1_out22), .Q(register_23_q), .clk(Clock), .clr(Clear));
  Register #(.width(32)) register_24 (.D(RW), .en(demultiplexer_1_out23), .Q(register_24_q), .clk(Clock), .clr(Clear));
  Register #(.width(32)) register_25 (.D(RW), .en(demultiplexer_1_out24), .Q(register_25_q), .clk(Clock), .clr(Clear));
  Register #(.width(32)) register_26 (.D(RW), .en(demultiplexer_1_out25), .Q(register_26_q), .clk(Clock), .clr(Clear));
  Register #(.width(32)) register_27 (.D(RW), .en(demultiplexer_1_out26), .Q(register_27_q), .clk(Clock), .clr(Clear));
  Register #(.width(32)) register_28 (.D(RW), .en(demultiplexer_1_out27), .Q(register_28_q), .clk(Clock), .clr(Clear));
  Register #(.width(32)) register_29 (.D(RW), .en(demultiplexer_1_out28), .Q(register_29_q), .clk(Clock), .clr(Clear));
  Register #(.width(32)) register_30 (.D(RW), .en(demultiplexer_1_out29), .Q(register_30_q), .clk(Clock), .clr(Clear));
  Register #(.width(32)) register_31 (.D(RW), .en(demultiplexer_1_out30), .Q(register_31_q), .clk(Clock), .clr(Clear));
  Register #(.width(32)) register_32 (.D(RW), .en(demultiplexer_1_out31), .Q(register_32_q), .clk(Clock), .clr(Clear));
  Multiplexer #(.select(5), .width(32), .enable("false")) multiplexer_2 (
    .in0(register_1_q), .in1(register_2_q), .in2(register_3_q), .in3(register_4_q), .in4(register_5_q),
    .in5(register_6_q), .in6(register_7_q), .in7(register_8_q), .in8(register_9_q), .in9(register_10_q),
    .in10(register_11_q), .in11(register_12_q), .in12(register_13_q), .in13(register_14_q),
    .in14(register_15_q), .in15(register_16_q), .in16(register_17_q), .in17(register_18_q),
    .in18(register_19_q), .in19(register_20_q), .in20(register_21_q), .in21(register_22_q),
    .in22(register_23_q), .in23(register_24_q), .in24(register_25_q), .in25(register_26_q),
    .in26(register_27_q), .in27(register_28_q), .in28(register_29_q), .in29(register_30_q),
    .in30(register_31_q), .in31(register_32_q), .out(Rs1), .sel(rs1_Select));
  Multiplexer #(.select(5), .width(32), .enable("false")) multiplexer_3 (
    .in0(register_1_q), .in1(register_2_q), .in2(register_3_q), .in3(register_4_q), .in4(register_5_q),
    .in5(register_6_q), .in6(register_7_q), .in7(register_8_q), .in8(register_9_q), .in9(register_10_q),
    .in10(register_11_q), .in11(register_12_q), .in12(register_13_q), .in13(register_14_q),
    .in14(register_15_q), .in15(register_16_q), .in16(register_17_q), .in17(register_18_q),
    .in18(register_19_q), .in19(register_20_q), .in20(register_21_q), .in21(register_22_q),
    .in22(register_23_q), .in23(register_24_q), .in24(register_25_q), .in25(register_26_q),
    .in26(register_27_q), .in27(register_28_q), .in28(register_29_q), .in29(register_30_q),
    .in30(register_31_q), .in31(register_32_q), .out(Rs2), .sel(rs2_Select));
endmodule

// Imm gen
module IMM_Generator (
  input  [11:0] imm,
  input  [19:0] U_imm,
  input  [31:0] PC,
  input  [6:0] Opcode,
  output [31:0] ImmOut
);

  wire comparator_1_eq, comparator_2_eq, comparator_3_eq, comparator_4_eq, comparator_5_eq;
  wire [1:0] multiplexer_2_out;
  wire [3:0] or_1_out;
  wire [31:0] adder_1_out, adder_2_out, bit_extender_1_out, bit_extender_2_out, lui_converter_1__32_lui;

  assign bit_extender_1_out = {{12{1'b0}}, U_imm};  // Bit_Extender bit_extender_1
  Adder_part #(.width(32)) adder_1 (.a(bit_extender_1_out), .b(PC), .out(adder_1_out));  // open: cin, cout
  assign bit_extender_2_out = {{20{1'b0}}, imm};  // Bit_Extender bit_extender_2
  Lui_Converter lui_converter_1 (.U_imm(U_imm), ._32_lui(lui_converter_1__32_lui));
  Comparator #(.width(7), .mode("unsigned")) comparator_1 (
    .a(Opcode), .b(7'b0000011), .eq(comparator_1_eq));  // open: gt, lt
  Comparator #(.width(7), .mode("unsigned")) comparator_2 (
    .a(Opcode), .b(7'b1100111), .eq(comparator_2_eq));  // open: gt, lt
  Comparator #(.width(7), .mode("unsigned")) comparator_3 (
    .a(Opcode), .b(7'b1100011), .eq(comparator_3_eq));  // open: gt, lt
  Comparator #(.width(7), .mode("unsigned")) comparator_4 (
    .a(Opcode), .b(7'b0100011), .eq(comparator_4_eq));  // open: gt, lt
  Comparator #(.width(7), .mode("unsigned")) comparator_5 (
    .a(Opcode), .b(7'b0010011), .eq(comparator_5_eq));  // open: gt, lt
  Comparator #(.width(7), .mode("unsigned")) comparator_6 (
    .a(Opcode), .b(7'b1101111), .eq(or_1_out[1]));  // open: gt, lt
  Comparator #(.width(7), .mode("unsigned")) comparator_7 (
    .a(Opcode), .b(7'b0110111), .eq(or_1_out[2]));  // open: gt, lt
  Comparator #(.width(7), .mode("unsigned")) comparator_8 (
    .a(Opcode), .b(7'b0010111), .eq(or_1_out[3]));  // open: gt, lt
  Adder_part #(.width(32)) adder_2 (.a(lui_converter_1__32_lui), .b(PC), .out(adder_2_out));  // open: cin, cout
  or or_1 (or_1_out[0], comparator_1_eq, comparator_2_eq, comparator_3_eq, comparator_4_eq, comparator_5_eq);
  Multiplexer #(.select(2), .width(32), .enable("false")) multiplexer_1 (
    .in0(bit_extender_2_out), .in1(adder_1_out), .in2(lui_converter_1__32_lui), .in3(adder_2_out),
    .out(ImmOut), .sel(multiplexer_2_out));
  Multiplexer #(.select(4), .width(2), .enable("false")) multiplexer_2 (
    .in1(2'b00), .in2(2'b01), .in4(2'b10), .in8(2'b11), .out(multiplexer_2_out), .sel(or_1_out));  // open: in0, in3, in5, in6, in7, in9, in10, in11, in12, in13, in14, in15
  // Probe on multiplexer_2_out

  // Notes on the sheet:
  //   I
  //   Jal
  //   Lui
  //   auipc
  //   Jal
  //   Lui
  //   Aui
endmodule

module ALU (
  input  [31:0] Rs1,
  input  [31:0] Rs2,
  input  Func7,
  input  [6:0] Opcode,
  input  [2:0] Func3,
  output [31:0] Out,
  output overflow,
  output Does_B
);

  wire b_type_alu_1_b, opcode_1_auipc, opcode_1_load, opcode_1_lui, opcode_1_store, opcode_2_sb_type,
       or_1_out;
  wire [2:0] demultiplexer_1_out0, demultiplexer_1_out1;
  wire [31:0] adder_1_out, r_i_type_alu_1_output;

  Adder_part #(.width(32)) adder_1 (.a(Rs1), .b(Rs2), .out(adder_1_out));  // open: cin, cout
  Opcode opcode_1 (
    .opcode(Opcode), .Load(opcode_1_load), .Store(opcode_1_store), .Lui(opcode_1_lui), .Auipc(opcode_1_auipc));  // open: R_Type, SB_Type, I_Type, JALR, JAL
  R_I_type_ALU r_i_type_alu_1 (
    .Func7_select(Func7), .S0(demultiplexer_1_out0[0]), .S1(demultiplexer_1_out0[1]),
    .S2(demultiplexer_1_out0[2]), .Rs1(Rs1), .Rs2(Rs2), .Output(r_i_type_alu_1_output), .Overflow(overflow));
  Multiplexer #(.width(32), .enable("false")) multiplexer_1 (
    .in0(r_i_type_alu_1_output), .in1(adder_1_out), .out(Out), .sel(or_1_out));
  or or_1 (or_1_out, opcode_1_load, opcode_1_store, opcode_1_lui, opcode_1_auipc);
  Opcode opcode_2 (
    .opcode(Opcode), .SB_Type(opcode_2_sb_type));  // open: R_Type, I_Type, Load, Store, JALR, JAL, Lui, Auipc
  Demultiplexer #(.width(3), .enable("false")) demultiplexer_1 (
    .out0(demultiplexer_1_out0), .out1(demultiplexer_1_out1), .in(Func3), .sel(opcode_2_sb_type));
  B_type_ALU b_type_alu_1 (
    .S0(demultiplexer_1_out1[0]), .S1(demultiplexer_1_out1[1]), .S2(demultiplexer_1_out1[2]), .RS1(Rs1),
    .RS2(Rs2), .B(b_type_alu_1_b));
  and and_1 (Does_B, opcode_2_sb_type, b_type_alu_1_b);
endmodule

module R_I_type_ALU (
  input  [31:0] Rs1,
  input  [31:0] Rs2,
  input  Func7_select,
  input  S0,
  input  S1,
  input  S2,
  output [31:0] Output,
  output Overflow
);

  wire comparator_1_lt, comparator_2_lt;
  wire [31:0] and_1_out, arithimatic_block_1_cout, bit_extender_1_out, bit_extender_2_out, multiplexer_1_out,
       multiplexer_2_out, multiplexer_3_out, multiplexer_5_out, multiplexer_6_out, multiplexer_7_out,
       or_1_out, shift_right_block_1_output, shifter_1_out, xor_1_out;

  Arithimatic_Block arithimatic_block_1 (
    .Rs1(Rs1), .Rs2(Rs2), .Select(Func7_select), .Cout(arithimatic_block_1_cout), .Overflow(Overflow));
  Shifter #(.width(32)) shifter_1 (.in(Rs1), .\dist (Rs2[4:0]), .out(shifter_1_out));
  Multiplexer #(.width(32), .enable("false")) multiplexer_1 (
    .in0(arithimatic_block_1_cout), .in1(shifter_1_out), .out(multiplexer_1_out), .sel(S0));
  Comparator #(.width(32)) comparator_1 (.a(Rs1), .b(Rs2), .lt(comparator_1_lt));  // open: gt, eq
  assign bit_extender_1_out = {{31{1'b0}}, comparator_1_lt};  // Bit_Extender bit_extender_1
  Multiplexer #(.width(32), .enable("false")) multiplexer_2 (
    .in0(multiplexer_1_out), .in1(multiplexer_3_out), .out(multiplexer_2_out), .sel(S1));
  Comparator #(.width(32), .mode("unsigned")) comparator_2 (.a(Rs1), .b(Rs2), .lt(comparator_2_lt));  // open: gt, eq
  Multiplexer #(.width(32), .enable("false")) multiplexer_3 (
    .in0(bit_extender_1_out), .in1(bit_extender_2_out), .out(multiplexer_3_out), .sel(S0));
  assign bit_extender_2_out = {{31{1'b0}}, comparator_2_lt};  // Bit_Extender bit_extender_2
  Multiplexer #(.width(32), .enable("false")) multiplexer_4 (
    .in0(multiplexer_2_out), .in1(multiplexer_7_out), .out(Output), .sel(S2));
  assign xor_1_out = Rs1 ^ Rs2;  // XOR_Gate xor_1, 32 bits wide
  Shift_Right_Block shift_right_block_1 (
    .Rs1(Rs1), .Rs2(Rs2), .Shift_right_Select(Func7_select), .Output(shift_right_block_1_output));
  Multiplexer #(.width(32), .enable("false")) multiplexer_5 (
    .in0(xor_1_out), .in1(shift_right_block_1_output), .out(multiplexer_5_out), .sel(S0));
  assign or_1_out = Rs1 | Rs2;  // OR_Gate or_1, 32 bits wide
  Multiplexer #(.width(32), .enable("false")) multiplexer_6 (
    .in0(or_1_out), .in1(and_1_out), .out(multiplexer_6_out), .sel(S0));
  Multiplexer #(.width(32), .enable("false")) multiplexer_7 (
    .in0(multiplexer_5_out), .in1(multiplexer_6_out), .out(multiplexer_7_out), .sel(S1));
  assign and_1_out = Rs1 & Rs2;  // AND_Gate and_1, 32 bits wide

  // Notes on the sheet:
  //   1
  //   2
  //   3
  //   4
  //   5
  //   6
  //   7
  //   8
endmodule

module B_type_ALU (
  input  [31:0] RS1,
  input  [31:0] RS2,
  input  S0,
  input  S1,
  input  S2,
  output B
);

  wire comparator_1_eq, comparator_2_eq, comparator_3_lt, comparator_4_eq, comparator_4_gt, comparator_5_lt,
       comparator_6_eq, comparator_6_gt, multiplexer_1_out, multiplexer_2_out, multiplexer_3_out,
       multiplexer_5_out, not_1_out, or_1_out, or_2_out;

  Comparator #(.width(32)) comparator_1 (.a(RS1), .b(RS2), .eq(comparator_1_eq));  // open: gt, lt
  Multiplexer #(.enable("false")) multiplexer_1 (
    .in0(comparator_1_eq), .in1(not_1_out), .out(multiplexer_1_out), .sel(S0));
  Comparator #(.width(32)) comparator_2 (.a(RS1), .b(RS2), .eq(comparator_2_eq));  // open: gt, lt
  not not_1 (not_1_out, comparator_2_eq);
  Comparator #(.width(32)) comparator_3 (.a(RS1), .b(RS2), .lt(comparator_3_lt));  // open: gt, eq
  Comparator #(.width(32)) comparator_4 (.a(RS1), .b(RS2), .gt(comparator_4_gt), .eq(comparator_4_eq));  // open: lt
  Multiplexer #(.enable("false")) multiplexer_2 (
    .in0(comparator_3_lt), .in1(or_1_out), .out(multiplexer_2_out), .sel(S0));
  or or_1 (or_1_out, comparator_4_eq, comparator_4_gt);
  Comparator #(.width(32), .mode("unsigned")) comparator_5 (.a(RS1), .b(RS2), .lt(comparator_5_lt));  // open: gt, eq
  Multiplexer #(.enable("false")) multiplexer_3 (
    .in0(multiplexer_2_out), .in1(multiplexer_5_out), .out(multiplexer_3_out), .sel(S1));
  Multiplexer #(.enable("false")) multiplexer_4 (.in0(multiplexer_1_out), .in1(multiplexer_3_out), .out(B), .sel(S2));
  Comparator #(.width(32), .mode("unsigned")) comparator_6 (
    .a(RS1), .b(RS2), .gt(comparator_6_gt), .eq(comparator_6_eq));  // open: lt
  Multiplexer #(.enable("false")) multiplexer_5 (
    .in0(comparator_5_lt), .in1(or_2_out), .out(multiplexer_5_out), .sel(S0));
  or or_2 (or_2_out, comparator_6_eq, comparator_6_gt);
endmodule

// Decoder
module Instruction_decoder (
  input  [31:0] Instruction,
  input  [31:0] PC,
  output [6:0] OPcode,
  output [4:0] RD,
  output [2:0] Func3,
  output [4:0] Rs1,
  output [4:0] Rs2,
  output [6:0] Func7,
  output [11:0] Imm,
  output [19:0] U_Imm
);

  wire [1:0] u_imm_control_1_out;
  wire [2:0] imm_control_1_out;
  wire [11:0] Jalr__imm;
  wire [19:0] Jal_imm;
  wire [31:0] adder_1_out, bit_extender_2_out;

  Imm_Control imm_control_1 (.opcode(Instruction[6:0]), .out(imm_control_1_out));
  Multiplexer #(.select(3), .width(12), .enable("false")) multiplexer_1 (
    .in0({Instruction[31:25], Instruction[14], Instruction[10:7]}), .in1(Instruction[31:20]),
    .in2(Instruction[31:20]), .in3({Instruction[31], Instruction[8], Instruction[30:25], Instruction[12:9]}),
    .in4(Jalr__imm), .out(Imm), .sel(imm_control_1_out));  // open: in5, in6, in7
  Bit_Extender #(.in_width(21), .out_width(20)) bit_extender_1 (
    .in({Instruction[31], Instruction[19:12], Instruction[20], Instruction[30:21], 1'b0}), .out(Jal_imm));
  U_imm_control u_imm_control_1 (.Opcode(Instruction[6:0]), .out(u_imm_control_1_out));
  Multiplexer #(.select(2), .width(20), .enable("false")) multiplexer_2 (
    .in0(Jal_imm), .in1(Instruction[31:12]), .in2(Instruction[31:12]), .out(U_Imm), .sel(u_imm_control_1_out));  // open: in3
  assign bit_extender_2_out = {{20{1'b0}}, Instruction[31:20]};  // Bit_Extender bit_extender_2
  Adder_part #(.width(32)) adder_1 (.a(bit_extender_2_out), .b(PC), .out(adder_1_out));  // open: cin, cout
  Bit_Extender #(.in_width(32), .out_width(12)) bit_extender_3 (.in(adder_1_out), .out(Jalr__imm));

  assign Func3 = Instruction[14:12];
  assign Func7 = Instruction[31:25];
  assign OPcode = Instruction[6:0];
  assign RD = Instruction[11:7];
  assign Rs1 = Instruction[19:15];
  assign Rs2 = Instruction[24:20];

  // Other names for the same wires on the sheet: B__imm[11:0] = {Instruction[31], Instruction[8], Instruction[30:25], Instruction[12:9]};
  //   S__imm[11:0] = {Instruction[31:25], Instruction[14], Instruction[10:7]}; F3[2:0] = Instruction[14:12];
  //   U_imm_Aui[19:0] = Instruction[31:12]; U_imm_Lui[19:0] = Instruction[31:12]; I__imm[11:0] = Instruction[31:20];
  //   L__imm[11:0] = Instruction[31:20]; F7[6:0] = Instruction[31:25]

  // Notes on the sheet:
  //   R Format
  //   I Format
  //   B Format
  //   Load
  //   Store
  //   Jal
  //   JalR
  //   Lui
  //   LUI
  //   Auipc
  //   AUI
endmodule

module Control_Unit (
  input  [6:0] Func7,
  input  Branch,
  input  [6:0] Opcode,
  output Imm_Enable,
  output Reg_Disable,
  output Load,
  output Store,
  output out
);

  wire not_1_out, not_2_out, not_3_out, not_4_out, not_5_out, not_6_out, opcode_1_auipc, opcode_1_i_type,
       opcode_1_jal, opcode_1_jalr, opcode_1_lui;

  not not_1 (not_1_out, Func7[0]);
  not not_2 (not_2_out, Func7[1]);
  not not_3 (not_3_out, Func7[2]);
  not not_4 (not_4_out, Func7[3]);
  not not_5 (not_5_out, Func7[4]);
  not not_6 (not_6_out, Func7[6]);
  and and_1 (out, not_1_out, not_2_out, not_3_out, not_4_out, not_5_out, Func7[5], not_6_out);
  or or_1 (Reg_Disable, Store, Branch);
  Opcode opcode_1 (
    .opcode(Opcode), .I_Type(opcode_1_i_type), .Load(Load), .Store(Store), .JALR(opcode_1_jalr),
    .JAL(opcode_1_jal), .Lui(opcode_1_lui), .Auipc(opcode_1_auipc));  // open: R_Type, SB_Type
  or or_2 (Imm_Enable, opcode_1_auipc, opcode_1_i_type, Load, Store, opcode_1_jalr, opcode_1_jal, opcode_1_lui);

  // Notes on the sheet:
  //   Reg Disable
endmodule

module Opcode (
  input  [6:0] opcode,
  output R_Type,
  output SB_Type,
  output I_Type,
  output Load,
  output Store,
  output JALR,
  output JAL,
  output Lui,
  output Auipc
);

  Comparator #(.width(7), .mode("unsigned")) comparator_1 (.a(7'b0110011), .b(opcode), .eq(R_Type));  // open: gt, lt
  Comparator #(.width(7), .mode("unsigned")) comparator_2 (.a(opcode), .b(7'b1100011), .eq(SB_Type));  // open: gt, lt
  Comparator #(.width(7), .mode("unsigned")) comparator_3 (.a(opcode), .b(7'b0010011), .eq(I_Type));  // open: gt, lt
  Comparator #(.width(7), .mode("unsigned")) comparator_4 (.a(opcode), .b(7'b0000011), .eq(Load));  // open: gt, lt
  Comparator #(.width(7), .mode("unsigned")) comparator_5 (.a(opcode), .b(7'b0100011), .eq(Store));  // open: gt, lt
  Comparator #(.width(7), .mode("unsigned")) comparator_6 (.a(opcode), .b(7'b1100111), .eq(JALR));  // open: gt, lt
  Comparator #(.width(7), .mode("unsigned")) comparator_7 (.a(opcode), .b(7'b1101111), .eq(JAL));  // open: gt, lt
  Comparator #(.width(7), .mode("unsigned")) comparator_8 (.a(opcode), .b(7'b0110111), .eq(Lui));  // open: gt, lt
  Comparator #(.width(7), .mode("unsigned")) comparator_9 (.a(opcode), .b(7'b0010111), .eq(Auipc));  // open: gt, lt
endmodule

module Imm_Control (
  input  [6:0] opcode,
  output [2:0] out
);

  wire [4:0] comparator_4_eq;

  Comparator #(.width(7), .mode("unsigned")) comparator_1 (
    .a(opcode), .b(7'b1100011), .eq(comparator_4_eq[3]));  // open: gt, lt
  Comparator #(.width(7), .mode("unsigned")) comparator_2 (
    .a(opcode), .b(7'b0010011), .eq(comparator_4_eq[2]));  // open: gt, lt
  Comparator #(.width(7), .mode("unsigned")) comparator_3 (
    .a(opcode), .b(7'b0000011), .eq(comparator_4_eq[1]));  // open: gt, lt
  Comparator #(.width(7), .mode("unsigned")) comparator_4 (
    .a(opcode), .b(7'b0100011), .eq(comparator_4_eq[0]));  // open: gt, lt
  Comparator #(.width(7), .mode("unsigned")) comparator_5 (
    .a(opcode), .b(7'b1100111), .eq(comparator_4_eq[4]));  // open: gt, lt
  Multiplexer #(.select(5), .width(3), .enable("false")) multiplexer_1 (
    .in1(3'b000), .in2(3'b001), .in4(3'b010), .in8(3'b011), .in16(3'b100), .out(out), .sel(comparator_4_eq));  // open: in0, in3, in5, in6, in7, in9, in10, in11, in12, in13, in14, in15, in17, in18, in19, in20, in21, in22, in23, in24, in25, in26, in27, in28, in29, in30, in31

  // Notes on the sheet:
  //   B
  //   I
  //   L
  //   s
  //   Jalr
endmodule

module U_imm_control (
  input  [6:0] Opcode,
  output [1:0] out
);

  wire [2:0] comparator_1_eq;

  Comparator #(.width(7), .mode("unsigned")) comparator_1 (
    .a(Opcode), .b(7'b1101111), .eq(comparator_1_eq[0]));  // open: gt, lt
  Comparator #(.width(7), .mode("unsigned")) comparator_2 (
    .a(Opcode), .b(7'b0110111), .eq(comparator_1_eq[1]));  // open: gt, lt
  Comparator #(.width(7), .mode("unsigned")) comparator_3 (
    .a(Opcode), .b(7'b0010111), .eq(comparator_1_eq[2]));  // open: gt, lt
  Multiplexer #(.select(3), .width(2), .enable("false")) multiplexer_1 (
    .in1(2'b00), .in2(2'b01), .in4(2'b10), .out(out), .sel(comparator_1_eq));  // open: in0, in3, in5, in6, in7

  // Notes on the sheet:
  //   Lui
  //   Jal
  //   Aui
endmodule

module PC (
  input  [11:0] Imm,
  input  [19:0] U_Imm,
  input  [6:0] Opcode,
  output [31:0] out
);

  wire [1:0] pc_control_1_out;
  wire [31:0] bit_extender_1_out, bit_extender_2_out, divider_1_out;

  assign bit_extender_1_out = {{20{1'b0}}, Imm};  // Bit_Extender bit_extender_1
  assign bit_extender_2_out = {{12{1'b0}}, U_Imm};  // Bit_Extender bit_extender_2
  Divider #(.width(32)) divider_1 (.a(bit_extender_2_out), .b(32'h4), .out(divider_1_out));  // open: upper, rem
  Divider #(.width(32)) divider_2 (.b(32'h4));  // open: a, out, upper, rem
  Multiplexer #(.select(2), .width(32), .enable("false")) multiplexer_1 (
    .in0(32'h1), .in1(bit_extender_1_out), .in2(divider_1_out), .in3(bit_extender_1_out), .out(out),
    .sel(pc_control_1_out));
  Pc_control pc_control_1 (.out(pc_control_1_out), .opcode(Opcode));
endmodule

module Pc_control (
  input  [6:0] opcode,
  output [1:0] out
);

  wire not_1_out, not_2_out, not_3_out;
  wire [3:0] and_1_out;

  Comparator #(.width(7), .mode("unsigned")) comparator_1 (
    .a(opcode), .b(7'b1100011), .eq(and_1_out[1]));  // open: gt, lt
  Comparator #(.width(7), .mode("unsigned")) comparator_2 (
    .a(opcode), .b(7'b1101111), .eq(and_1_out[2]));  // open: gt, lt
  Comparator #(.width(7), .mode("unsigned")) comparator_3 (
    .a(opcode), .b(7'b1100111), .eq(and_1_out[3]));  // open: gt, lt
  not not_1 (not_1_out, and_1_out[1]);
  not not_2 (not_2_out, and_1_out[2]);
  not not_3 (not_3_out, and_1_out[3]);
  and and_1 (and_1_out[0], not_1_out, not_2_out, not_3_out);
  Multiplexer #(.select(4), .width(2), .enable("false")) multiplexer_1 (
    .in1(2'b00), .in2(2'b01), .in4(2'b10), .in8(2'b11), .out(out), .sel(and_1_out));  // open: in0, in3, in5, in6, in7, in9, in10, in11, in12, in13, in14, in15

  // Notes on the sheet:
  //   B
  //   Jal
  //   Jalr
endmodule

module Arithimatic_Block (
  input  [31:0] Rs1,
  input  [31:0] Rs2,
  input  Select,
  output [31:0] Cout,
  output Overflow
);

  wire adder_1_cout, subtractor_1_bout;
  wire [31:0] adder_1_out, subtractor_1_out;

  Adder_part #(.width(32)) adder_1 (.a(Rs1), .b(Rs2), .out(adder_1_out), .cout(adder_1_cout));  // open: cin
  Subtractor #(.width(32)) subtractor_1 (
    .a(Rs1), .b(Rs2), .out(subtractor_1_out), .bout(subtractor_1_bout));  // open: bin
  Multiplexer #(.width(32), .enable("false")) multiplexer_1 (
    .in0(adder_1_out), .in1(subtractor_1_out), .out(Cout), .sel(Select));
  Multiplexer #(.enable("false")) multiplexer_2 (
    .in0(adder_1_cout), .in1(subtractor_1_bout), .out(Overflow), .sel(Select));

  // Notes on the sheet:
  //   ADD
  //   Sub
endmodule

module Shift_Right_Block (
  input  [31:0] Rs1,
  input  [31:0] Rs2,
  input  Shift_right_Select,
  output [31:0] Output
);

  wire [31:0] shifter_1_out, shifter_2_out;

  Shifter #(.width(32), .shift("lr")) shifter_1 (.in(Rs1), .\dist (Rs2[4:0]), .out(shifter_1_out));
  Shifter #(.width(32), .shift("ar")) shifter_2 (.in(Rs1), .\dist (Rs2[4:0]), .out(shifter_2_out));
  Multiplexer #(.width(32), .enable("false")) multiplexer_1 (
    .in0(shifter_1_out), .in1(shifter_2_out), .out(Output), .sel(Shift_right_Select));

  // Notes on the sheet:
  //   Shift Right Logical
  //   Shift Right Arithimatic
endmodule

module Adder (
  input  [31:0] in_1,
  input  [31:0] in_2,
  output [31:0] out_3
);

  Adder_part #(.width(32)) adder_1 (.a(in_1), .b(in_2), .out(out_3));  // open: cin, cout
endmodule

module Extender (
  input  [31:0] in,
  output [23:0] out
);

  Bit_Extender #(.in_width(32), .out_width(24)) bit_extender_1 (.in(in), .out(out));
endmodule

module Lui_Converter (
  input  [19:0] U_imm,
  output [31:0] _32_lui
);


  assign _32_lui = {U_imm, {12{1'b0}}};
endmodule
